# Fritzing sketch PneumaticControl (saved by Fritzing 0.9.3b)
circuit board: 5cm x 7cm
breadboards: 4

parts:
  Feather_ESP32 = Adafruit HUZZAH32 ESP32 Feather [part_number="Adafruit #3405"]
  UA78M33C = Voltage Regulator - 3.3V [package="TO220 [THT]"]
  TIP120 = npn-Powertransistor [package="TO220 [THT]"]
  TIP120_2 = npn-Powertransistor [package="TO220 [THT]"]
  TIP120_3 = npn-Powertransistor [package="TO220 [THT]"]
  J2 = Screw terminal - 2 pins [package=THT]
  J3 = Screw terminal - 2 pins [package=THT]
  J4 = Screw terminal - 2 pins [package=THT]
  D4 = Rectifier Diode [part_number=1N4001 package="300 mil [THT]"]
  D3 = Rectifier Diode [part_number=1N4001 package="300 mil [THT]"]
  D2 = Rectifier Diode [part_number=1N4001 package="300 mil [THT]"]
  D1 = Rectifier Diode [part_number=1N4001 package="300 mil [THT]"]
  R4 = Resistor [tolerance=±5% resistance=1k package=THT]
  R3 = Resistor [tolerance=±5% resistance=1k package=THT]
  R2 = Resistor [tolerance=±5% resistance=1k package=THT]
  R1 = Resistor [tolerance=±5% resistance=1k package=THT]
  J1 = Screw terminal - 2 pins [package=THT]
  C1-220mu = Electrolytic Capacitor [capacitance=0.22mF voltage=16V package="100 mil [THT, electrolytic]"]
  C2-47mu = Electrolytic Capacitor [capacitance=47µF voltage=16V package="100 mil [THT, electrolytic]"]
  D5 = Rectifier Diode [part_number=1N4001 package="300 mil [THT]"]
  J5 = Screw terminal - 2 pins [package=THT]
  LM7809 = Voltage Regulator - 5V [package="TO220 [THT]"]
  C3-0_47m = Electrolytic Capacitor [capacitance=0.47mF voltage=10V package="100 mil [THT, electrolytic]"]
  C4-0_1m = Electrolytic Capacitor [capacitance=0.1mF voltage=10V package="100 mil [THT, electrolytic]"]
  TIP120_4 = npn-Powertransistor [package="TO220 [THT]"]

nets:
  GND: Feather_ESP32.GND, UA78M33C.GND, TIP120.emitter, TIP120_2.emitter, TIP120_3.emitter, C1-220mu.-, C2-47mu.-, J5.pin2, LM7809.GND, C3-0_47m.-, C4-0_1m.-, TIP120_4.emitter
  N1: Feather_ESP32.VBAT, UA78M33C.output_voltage, C4-0_1m.+
  N2: Feather_ESP32.IO27_A10, R1.Pin_1
  N3: Feather_ESP32.IO15_A8, R3.Pin_1
  N4: Feather_ESP32.IO32_A7, R4.Pin_1
  N5: Feather_ESP32.IO14_A6, R2.Pin_1
  N6: UA78M33C.input_voltage, J2.pin1, J3.pin1, J4.pin1, D4.cathode, D3.cathode, D2.cathode, D1.cathode, J1.pin1, C2-47mu.+, LM7809.output_voltage, C3-0_47m.+
  N7: TIP120.base, R2.Pin_0
  N8: TIP120.collector, J2.pin2, D2.anode
  N9: TIP120_2.base, R3.Pin_0
  N10: TIP120_2.collector, J3.pin2, D3.anode
  N11: TIP120_3.base, R4.Pin_0
  N12: TIP120_3.collector, J4.pin2, D4.anode
  N13: D1.anode, J1.pin2, TIP120_4.collector
  N14: R1.Pin_0, TIP120_4.base
  N15: C1-220mu.+, D5.cathode, LM7809.input_voltage
  N16: D5.anode, J5.pin1

notes:
  GND/12V
  -/+
